// Digital circuit control_bomba.dig as structural Verilog
module control_bomba (
  input  tanqueH,
  input  tanqueL,
  input  cisternaOK,
  input  cisternaL,
  output bomba
);

  wire not_1_out, not_2_out, rs_ff_as_1_q, rs_ff_as_2_nq;

  not not_1 (not_1_out, tanqueL);
  not not_2 (not_2_out, cisternaL);
  RS_FF_AS rs_ff_as_1 (.S(not_1_out), .R(tanqueH), .Q(rs_ff_as_1_q));  // open: nQ
  RS_FF_AS rs_ff_as_2 (.S(not_2_out), .R(cisternaOK), .nQ(rs_ff_as_2_nq));  // open: Q
  and and_1 (bomba, rs_ff_as_1_q, rs_ff_as_2_nq);
endmodule
