// Digital circuit unidad_aritmetica_logica.dig as structural Verilog
module unidad_aritmetica_logica (
  input  invB,
  input  logica,
  input  \and ,
  input  [15:0] A,
  input  [15:0] B,
  output [15:0] R
);

  wire [15:0] add_1_s, and_1_out, and_2_out, not_1_out, not_2_out, or_1_out, or_2_out, sub_1_s;

  Add #(.Bits(16)) add_1 (.a(A), .b(B), .c_i(1'b0), .s(add_1_s));  // open: c_o
  assign or_1_out = A | B;  // Or or_1, 16 bits wide
  assign and_1_out = A & B;  // And and_1, 16 bits wide
  Sub #(.Bits(16)) sub_1 (.a(A), .b(B), .c_i(1'b0), .s(sub_1_s));  // open: c_o
  assign or_2_out = A | not_1_out;  // Or or_2, 16 bits wide
  assign not_1_out = ~B;  // Not not_1, 16 bits wide
  assign and_2_out = A & not_2_out;  // And and_2, 16 bits wide
  assign not_2_out = ~B;  // Not not_2, 16 bits wide
  Multiplexer #(.Selector_Bits(3), .Bits(16)) multiplexer_1 (
    .sel({invB, logica, \and }), .in_0(add_1_s), .in_1(add_1_s), .in_2(or_1_out), .in_3(and_1_out),
    .in_4(sub_1_s), .in_5(sub_1_s), .in_6(or_2_out), .in_7(and_2_out), .out(R));
endmodule
